# Fritzing sketch RAM-16 (saved by Fritzing 0.9.6b)
circuit board: 8.46667cm x 5.64444cm
breadboards: 4

parts:
  U3 = 74HC245 [package="DIP (Dual Inline) [THT]"]
  U4 = 74HC245 [package="DIP (Dual Inline) [THT]"]
  U7 = 74HC20 [package="DIP (Dual Inline) [THT]"]
  U8 = 74HC00 [package="DIP (Dual Inline) [THT]"]
  U9 = 74HC08 [package="DIP (Dual Inline) [THT]"]
  U10 = 74HC139 [package="DIP (Dual Inline) [THT]"]
  U11 = AS6C6264 [package="DIP (Dual Inline) [THT]"]
  U12 = AS6C6264 [package="DIP (Dual Inline) [THT]"]
  U13 = AS6C6264 [package="DIP (Dual Inline) [THT]"]
  U14 = AS6C6264 [package="DIP (Dual Inline) [THT]"]
  U17 = 74HC245 [package="DIP (Dual Inline) [THT]"]
  U18 = 74HC157 [package="DIP (Dual Inline) [THT]"]
  U19 = 74HC32 [package="DIP (Dual Inline) [THT]"]
  U20 = DIP - 16 pins [chip_label=82ohm package="DIP (Dual Inline) [THT]"]
  U21 = DIP - 16 pins [chip_label=82ohm package="DIP (Dual Inline) [THT]"]
  U22 = DIP - 16 pins [chip_label=82ohm package="DIP (Dual Inline) [THT]"]
  U23 = DIP - 16 pins [chip_label=82ohm package="DIP (Dual Inline) [THT]"]
  U24 = 74HC32 [package="DIP (Dual Inline) [THT]"]

nets:
  N1: U3.DIR, U4.DIR, U8.4A, U8.4B, U10.1A0, U10.2A1, U17.DIR, U18.1in0, U18.2in0, U20.pin1, U21.pin8
  N2: U3.A1, U3.A8
  GND: U3.GND, U4.GND, U13.A0, U13.Vss, U14.A0, U17.GND
  N3: U3.B8, U3.B1
  N4: U3./DIR, U17./DIR, U19.3Y
  VCC: U3.Vcc, U4.Vcc, U17.Vcc
  N5: U4.A1, U4.A8
  N6: U4.B8, U4.B1
  N7: U4./DIR, U19.4Y
  N8: U7.1A, U7.1D
  N9: U7.NC#2, U20.pin14
  N10: U7.1Y, U8.1B, U8.2B, U10.1A1, U11.CE2, U12.CE2, U13.CE2, U14.CE2
  N11: U7.2Y, U21.pin14
  N12: U7.2A, U7.2D
  N13: U7.NC#10, U20.pin7
  N14: U8.1A, U9.3Y
  N15: U8.1Y, U24.4A
  N16: U8.2A, U8.3Y
  N17: U8.2Y, U24.3A
  GND_2: U8.GND, U9.1A, U9.1B, U9.2A, U9.2B, U9.GND, U10.1E#, U10.GND, U18.GND
  N18: U8.3A, U9.3B, U11.A0, U12.A0, U18.S
  N19: U8.3B, U9.3A, U10.2A0, U20.pin2
  N20: U8.4Y, U18.3in0, U18.4in0
  VCC_2: U8.Vcc, U9.Vcc, U10.VCC, U11.DQ0, U11.DQ7, U11.Vcc, U12.Vcc, U18.VCC, U24.Vcc
  N21: U9.4Y, U24.2A
  N22: U10.1Y2#, U19.2A
  N23: U10.1Y3#, U19.1B
  N24: U10.2Y3#, U18.4in1
  N25: U10.2Y2#, U18.3in1
  N26: U10.2Y1#, U18.2in1
  N27: U10.2Y0#, U18.1in1
  N28: U11.A12, U11.A1
  VSS: U11.Vss, U12.Vss, U24.GND
  N29: U11./CE, U11.A8, U18.4Y#
  N30: U11./OE, U12./OE, U13./OE, U14./OE, U19.1Y
  N31: U11./WE, U12./WE, U13./WE, U14./WE, U19.2Y
  N32: U12.A12, U12.A1
  N33: U12.DQ0, U12.A8
  N34: U12./CE, U18.2Y#
  N35: U13.A12, U13.A1
  VCC_3: U13.DQ0, U13.DQ7, U13.Vcc, U14.Vcc
  N36: U13./CE, U13.A8, U18.1Y#
  N37: U14.A12, U14.A1
  N38: U14.DQ0, U14.A8
  N39: U14./CE, U18.3Y#
  N40: U17.A1, U17.A8
  N41: U17.B8, U17.B1
  N42: U18.E#, U19.GND
  N43: U19.1A, U19.2B, U19.3A, U19.4A, U24.1A, U24.2B
  N44: U19.3B, U24.3Y
  N45: U19.4B, U24.4Y
  N46: U20.pin6, U21.pin1
  N47: U20.pin12, U20.pin15, U20.pin16, U21.pin9
  N48: U22.pin1, U23.pin8
  N49: U22.pin16, U23.pin9
  N50: U24.3B, U24.4B

notes:
  Mem LB
  Sys LB
  Mem HB
  Sys LB
  Mem HB
  Sys HB
  HRLB
  LRLB
  HRHB
  LRHB
  Notes:
  HB, LB = High Byte, Low Byte
  Even bytes are low.
  HR, LR = High Range, Low Range. Byte addresses less than 16k are low range.
  Low byte RAM have A0 connected to ground. High byte RAMs have A0 connected to power.
  Transceivers connect memory bus LB to system bus LB ("Mem LB Sys LB"), or memory bus HB to system bus LB (for byte reads of odd addresses) or memory bus HB to system bus HB for the upper half of 16 bit reads.
  The white net is the RAM/IO# signal. The light brown net is the MEMRD# signal.
  The 7432 at upper left is a kludge, a fix for a mistake - the original design just enabled the memory on the bus for *every* cycle, like nothing else could ever drive the bus. ;-) Now the gray line has to be low; it's MEM_EN#. Else the transceivers are not enabled (dark brown wires to pin 19 of the 3 transceivers). MEM_EN# comes from the SYSDATA_SRC decoder in Central which decodes the K reg.
  The teal wire from the 6-pin connector at top to a 7408 is NANO_IR_EN#, MCR bit 0x02. The other teal wire is IR_CLK_EN# from the K reg. The 7408 forms a negative-true OR gate. The output mixes with SYSCLK at the left 7432, B unit (pins 4, 5, 6).
  Finally the A unit of that 7432 mixes the read signal for the IR with sysclk. This is hidden in the extreme lower right corner of the YARC Memory schematic in KiCad.

custom parts:
  74HC245: 8-bit bidrectional transceiver with straight-across pinout
  74HC20: Dual 4-input NAND gate
  74HC00: Quad NAND. The original 74xx part.
  74HC08: Quad positive AND gate
  74HC139: Dual 2-to-4 decoders with active low enable
  AS6C6264: 8k x 8 bit CMOS static RAM
  74HC157: Quad 2:1 mux
  74HC32: Quad 2-input OR gate
  DIP - 16 pins: A DIP stand-in part for whatever IC you want. With 16 pins on a 300mil dual inline package (DIP) footprint.
