# Fritzing sketch Registers (saved by Fritzing 0.9.6b)
breadboards: 6

parts:
  U1 = 74HC670 [package="DIP (Dual Inline) [THT]"]
  U2 = 74HC670 [package="DIP (Dual Inline) [THT]"]
  U3 = 74HC670 [package="DIP (Dual Inline) [THT]"]
  U4 = 74HC670 [package="DIP (Dual Inline) [THT]"]
  U5 = 74HC670 [package="DIP (Dual Inline) [THT]"]
  U6 = 74HC670 [package="DIP (Dual Inline) [THT]"]
  U7 = 74HC670 [package="DIP (Dual Inline) [THT]"]
  U8 = 74HC670 [package="DIP (Dual Inline) [THT]"]
  U9 = 74HC245 [package="DIP (Dual Inline) [THT]"]  # not connected
  U10 = 74HC245 [package="DIP (Dual Inline) [THT]"]  # not connected
  U11 = 74HC245 [package="DIP (Dual Inline) [THT]"]  # not connected
  U12 = 74HC245 [package="DIP (Dual Inline) [THT]"]  # not connected
  U13 = 74HC157 [package="DIP (Dual Inline) [THT]"]  # not connected
  U14 = 74HC157 [package="DIP (Dual Inline) [THT]"]  # not connected
  U15 = 74HC157 [package="DIP (Dual Inline) [THT]"]  # not connected
  U16 = 74HC157 [package="DIP (Dual Inline) [THT]"]  # not connected
  U17 = 74HC245 [package="DIP (Dual Inline) [THT]"]
  U18 = 74HC245 [package="DIP (Dual Inline) [THT]"]
  U19 = 74HC00 [package="DIP (Dual Inline) [THT]"]

nets:
  N1: U1.D3, U1.D0
  N2: U1.RA1, U2.RA1, U3.RA1, U4.RA1
  N3: U1.RA0, U2.RA0, U3.RA0, U4.RA0
  N4: U1.Q3, U1.Q1
  GND: U1.GND, U2.GND, U3.GND, U4.GND
  N5: U1.RE#, U2.RE#, U3.RE#, U4.RE#
  N6: U1.WE#, U1.WA0
  N7: U1.WA1, U2.WA1, U3.WA1, U4.WA1, U5.WA1, U6.WA1, U7.WA1, U8.WA1
  VCC: U1.Vcc, U2.Vcc, U3.Vcc, U4.Vcc
  N8: U2.D3, U2.D0
  N9: U2.Q3, U2.Q1
  N10: U2.WE#, U2.WA0
  N11: U3.D3, U3.D0
  N12: U3.Q3, U3.Q1
  N13: U3.WE#, U3.WA0
  N14: U4.D3, U4.D0
  N15: U4.Q3, U4.Q1
  N16: U4.WE#, U4.WA0
  N17: U5.D3, U5.D0
  N18: U5.RA1, U6.RA1, U7.RA1, U8.RA1
  N19: U5.RA0, U6.RA0, U7.RA0, U8.RA0
  N20: U5.Q3, U5.Q0
  GND_2: U5.GND, U6.GND, U7.GND, U8.GND
  N21: U5.RE#, U6.RE#, U7.RE#, U8.RE#
  N22: U5.WE#, U5.WA0
  N23: U6.D3, U6.D0
  N24: U6.Q3, U6.Q1
  N25: U6.WE#, U6.WA0
  VCC_2: U6.Vcc, U7.Vcc, U8.Vcc
  N26: U7.D3, U7.D0
  N27: U7.Q3, U7.Q0
  N28: U7.WE#, U7.WA0
  N29: U8.D3, U8.D0
  N30: U8.Q3, U8.Q0
  N31: U8.WE#, U8.WA0
  GND_3: U17.DIR, U17.GND, U18.DIR, U18.GND, U19.GND
  N32: U17.B8, U17.B7, U17.B6, U17.B5, U17.B4, U17.B3, U17.B2, U17.B1, U18.B6, U18.B5, U18.B4, U18.B3, U18.B2, U18.B1
  VCC_3: U18.Vcc, U19.Vcc

notes:
  src2 1:0 src2_sxt src2 :0 :1 :2

custom parts:
  74HC670: 4x4 bit register file
  74HC245: 8-bit bidrectional transceiver with straight-across pinout
  74HC157: Quad 2:1 mux
  74HC00: Quad NAND. The original 74xx part.
